# Fritzing sketch Turret (saved by Fritzing 0.9.3b)
perfboards: 1

parts:
  J1 = female pin header, 3 pins [form="♀ (female)"]
  J2 = female pin header, 3 pins [form="♀ (female)"]
  J3 = female pin header, 3 pins [form="♀ (female)"]
  Part1 = Arduino Nano (Rev3.0) (ICSP)

nets:
  N1: J1.pin1, Part1.D5
  N2: J1.pin2, J2.pin2, J3.pin2, Part1.GND
  N3: J1.pin3, J2.pin3, J3.pin3
  N4: J2.pin1, Part1.D6
  N5: J3.pin1, Part1.VIN
